// Logisim project decoder.circ as structural Verilog: 1 circuit, main circuit main
module main (
  input  in_1,
  input  in_2,
  input  in_3,
  input  x,
  input  y,
  input  z,
  input  in_7,
  input  in_8,
  input  in_9,
  input  in_10,
  input  in_11,
  input  in_12,
  input  in_13,
  input  in_14,
  input  in_15,
  input  in_16,
  input  in_17,
  input  in_18
);

  wire and_1_out, and_2_out, and_3_out, and_4_out, and_5_out, not_1_out, not_2_out, not_3_out, not_4_out,
       not_5_out, not_6_out, not_7_out, not_8_out, or_1_out, or_2_out, or_3_out;

  not not_1 (not_1_out, x);
  or or_1 (or_1_out, y, z);
  not not_2 (not_2_out, in_7);
  not not_3 (not_3_out, in_16);
  not not_4 (not_4_out, in_17);
  and and_1 (and_1_out, or_1_out, not_1_out);
  _7_Segment_Display u_7_segment_display_1 (.c(not_2_out));  // open: g, f, a, b, e, d, dp
  not not_5 (not_5_out, in_18);
  or or_2 (or_2_out, not_4_out, not_5_out);
  _7_Segment_Display u_7_segment_display_2 (.a(and_1_out));  // open: g, f, b, e, d, c, dp
  _7_Segment_Display u_7_segment_display_3 (.e(and_2_out));  // open: g, f, a, b, d, c, dp
  and and_2 (and_2_out, or_2_out, not_3_out);
  _7_Segment_Display u_7_segment_display_4 (.g(1'b1));  // open: f, a, b, e, d, c, dp
  not not_6 (not_6_out, in_1);
  and and_3 (and_3_out, not_6_out, in_2);
  not not_7 (not_7_out, in_11);
  and and_4 (and_4_out, not_7_out, in_12);
  not not_8 (not_8_out, in_13);
  or or_3 (or_3_out, in_14, in_15);
  _7_Segment_Display u_7_segment_display_5 (.b(and_3_out));  // open: g, f, a, e, d, c, dp
  and and_5 (and_5_out, or_3_out, not_8_out);
  _7_Segment_Display u_7_segment_display_6 (.d(and_4_out));  // open: g, f, a, b, e, c, dp
  _7_Segment_Display u_7_segment_display_7 (.f(and_5_out));  // open: g, a, b, e, d, c, dp

  // Notes on the sheet:
  //   Segment A
  //   Segment C
  //   Segment E
  //   Segment G
  //   Segment B
  //   Segment D
  //   Segment F
endmodule
